// Logisim project 2_1.circ as structural Verilog: 1 circuit, main circuit main
module main (
  input  in_1,
  input  in_2,
  input  in_3,
  input  in_4,
  input  in_5,
  input  in_6,
  input  in_7,
  input  in_8,
  input  in_9,
  input  in_10,
  input  in_11,
  input  in_12,
  input  in_13,
  input  in_14,
  input  in_15,
  input  in_16,
  input  in_17,
  input  in_18,
  input  in_19,
  input  in_20,
  input  in_21,
  input  in_22,
  input  in_23,
  input  in_24,
  input  in_25,
  input  in_26,
  input  in_27,
  input  in_28,
  input  in_29,
  input  in_30,
  input  in_31,
  input  in_32,
  input  in_33,
  output out_34,
  output out_35,
  output out_36,
  output out_37,
  output out_38,
  output out_39,
  output out_40,
  output out_41,
  output out_42,
  output out_43,
  output out_44,
  output out_45,
  output out_46,
  output out_47,
  output out_48,
  output out_49,
  output out_50,
  output out_51,
  output out_52,
  output out_53,
  output out_54,
  output out_55,
  output out_56,
  output out_57
);

  and and_1 (out_38, in_5, in_7);
  and and_2 (out_41, in_9, in_10);
  and and_3 (out_44, in_12, in_14);
  and and_4 (out_47, in_16, in_18);
  and and_5 (out_50, in_20, in_22);
  and and_6 (out_53, in_24, in_26);
  and and_7 (out_56, in_28, in_30);
  and and_8 (out_57, in_32, in_33);
  and and_9 (out_34, in_1, in_2);
  and and_10 (out_36, in_3, in_4);
  and and_11 (out_39, in_6, in_8);
  and and_12 (out_42, in_11, in_13);
  and and_13 (out_45, in_15, in_17);
  and and_14 (out_48, in_19, in_21);
  and and_15 (out_51, in_23, in_25);
  and and_16 (out_54, in_27, in_29);
  assign out_35 = in_31 ? out_34 : 1'bz;  // Controlled_Buffer controlled_buffer_1
  assign out_37 = in_31 ? out_36 : 1'bz;  // Controlled_Buffer controlled_buffer_2
  assign out_40 = in_31 ? out_39 : 1'bz;  // Controlled_Buffer controlled_buffer_3
  assign out_43 = in_31 ? out_42 : 1'bz;  // Controlled_Buffer controlled_buffer_4
  assign out_46 = in_31 ? out_45 : 1'bz;  // Controlled_Buffer controlled_buffer_5
  assign out_49 = in_31 ? out_48 : 1'bz;  // Controlled_Buffer controlled_buffer_6
  assign out_52 = in_31 ? out_51 : 1'bz;  // Controlled_Buffer controlled_buffer_7
  assign out_55 = in_31 ? out_54 : 1'bz;  // Controlled_Buffer controlled_buffer_8
endmodule
