// Logisim project 2_2.circ as structural Verilog
module main (
  input  in_1,
  input  in_2,
  input  in_3,
  input  in_4,
  input  in_5,
  input  in_6,
  input  in_7,
  input  in_8,
  input  in_9,
  input  in_10,
  input  in_11,
  input  in_12,
  input  in_13,
  input  in_14,
  input  in_15,
  input  in_16,
  input  in_17,
  input  in_18,
  input  in_19,
  input  in_20,
  input  in_21,
  input  in_22,
  input  in_23,
  input  in_24,
  input  in_25,
  input  in_26,
  input  in_27,
  input  in_28,
  input  in_29,
  input  in_30,
  input  in_31,
  input  in_32,
  input  in_33,
  output out_34,
  output out_35,
  output out_36,
  output out_37,
  output out_38,
  output out_39,
  output out_40,
  output out_41,
  output out_42,
  output out_43,
  output out_44,
  output out_45,
  output out_46,
  output out_47,
  output out_48,
  output out_49,
  output out_50,
  output out_51,
  output out_52,
  output out_53,
  output out_54,
  output out_55,
  output out_56,
  output out_57
);

  or or_1 (out_34, in_1, in_3);
  or or_2 (out_37, in_5, in_7);
  or or_3 (out_42, in_10, in_12);
  or or_4 (out_45, in_14, in_16);
  or or_5 (out_48, in_18, in_20);
  or or_6 (out_51, in_22, in_24);
  or or_7 (out_54, in_26, in_28);
  or or_8 (out_57, in_30, in_33);
  or or_9 (out_35, in_2, in_4);
  or or_10 (out_38, in_6, in_8);
  or or_11 (out_40, in_9, in_11);
  or or_12 (out_43, in_13, in_15);
  or or_13 (out_46, in_17, in_19);
  or or_14 (out_49, in_21, in_23);
  or or_15 (out_52, in_25, in_27);
  or or_16 (out_55, in_29, in_31);
  assign out_36 = in_32 ? out_35 : 1'bz;  // Controlled_Buffer controlled_buffer_1
  assign out_39 = in_32 ? out_38 : 1'bz;  // Controlled_Buffer controlled_buffer_2
  assign out_41 = in_32 ? out_40 : 1'bz;  // Controlled_Buffer controlled_buffer_3
  assign out_44 = in_32 ? out_43 : 1'bz;  // Controlled_Buffer controlled_buffer_4
  assign out_47 = in_32 ? out_46 : 1'bz;  // Controlled_Buffer controlled_buffer_5
  assign out_50 = in_32 ? out_49 : 1'bz;  // Controlled_Buffer controlled_buffer_6
  assign out_53 = in_32 ? out_52 : 1'bz;  // Controlled_Buffer controlled_buffer_7
  assign out_56 = in_32 ? out_55 : 1'bz;  // Controlled_Buffer controlled_buffer_8
endmodule
