// Logisim project 2_3.circ as structural Verilog: 1 circuit, main circuit main
module main (
  input  in_1,
  input  in_2,
  input  in_3,
  input  in_4,
  input  in_5,
  input  in_6,
  input  in_7,
  input  in_8,
  input  in_9,
  input  in_10,
  input  in_11,
  input  in_12,
  input  in_13,
  input  in_14,
  input  in_15,
  input  in_16,
  input  in_17,
  output out_18,
  output out_19,
  output out_20,
  output out_21,
  output out_22,
  output out_23,
  output out_24,
  output out_25,
  output out_26,
  output out_27,
  output out_28,
  output out_29,
  output out_30,
  output out_31,
  output out_32,
  output out_33,
  output out_34,
  output out_35,
  output out_36,
  output out_37,
  output out_38,
  output out_39,
  output out_40,
  output out_41
);

  not not_1 (out_18, in_1);
  not not_2 (out_21, in_3);
  not not_3 (out_26, in_6);
  not not_4 (out_31, in_9);
  not not_5 (out_36, in_12);
  not not_6 (out_39, in_14);
  not not_7 (out_40, in_16);
  not not_8 (out_41, in_17);
  not not_9 (out_19, in_2);
  not not_10 (out_22, in_4);
  not not_11 (out_24, in_5);
  not not_12 (out_27, in_7);
  not not_13 (out_29, in_8);
  not not_14 (out_32, in_10);
  not not_15 (out_34, in_11);
  not not_16 (out_37, in_13);
  assign out_20 = in_15 ? out_19 : 1'bz;  // Controlled_Buffer controlled_buffer_1
  assign out_23 = in_15 ? out_22 : 1'bz;  // Controlled_Buffer controlled_buffer_2
  assign out_25 = in_15 ? out_24 : 1'bz;  // Controlled_Buffer controlled_buffer_3
  assign out_28 = in_15 ? out_27 : 1'bz;  // Controlled_Buffer controlled_buffer_4
  assign out_30 = in_15 ? out_29 : 1'bz;  // Controlled_Buffer controlled_buffer_5
  assign out_33 = in_15 ? out_32 : 1'bz;  // Controlled_Buffer controlled_buffer_6
  assign out_35 = in_15 ? out_34 : 1'bz;  // Controlled_Buffer controlled_buffer_7
  assign out_38 = in_15 ? out_37 : 1'bz;  // Controlled_Buffer controlled_buffer_8
endmodule
