// Logisim project 4x1mux.circ as structural Verilog: 2 circuits, main circuit main
module main (
  input  in_1,
  input  in_2,
  input  in_3,
  input  in_4,
  input  in_5,
  input  in_6,
  output out_7
);

  wire and_1_out, and_2_out, and_3_out, and_4_out, not_1_out, not_2_out;

  not not_1 (not_1_out, in_6);
  not not_2 (not_2_out, in_5);
  and and_1 (and_1_out, in_1, not_1_out, not_2_out);
  and and_2 (and_2_out, in_2, not_2_out, in_6);
  and and_3 (and_3_out, in_3, in_5, not_1_out);
  and and_4 (and_4_out, in_4, in_5, in_6);
  or or_1 (out_7, and_1_out, and_2_out, and_3_out, and_4_out);
endmodule

module _4_1mux (
  input  in_1,
  input  in_2,
  output out_3,
  output out_4,
  output out_5,
  output out_6,
  output out_7
);

  and and_1 (out_3, in_1, in_2);
  or or_1 (out_4, in_1, in_2);
  not not_1 (out_6, in_1);
  xor xor_1 (out_7, in_1, in_2);
  main main_1 (.in_1(out_3), .in_2(out_4), .in_3(out_6), .in_4(out_7), .out_7(out_5));  // open: in_5, in_6
endmodule
