// Logisim project 5.circ as structural Verilog: 4 circuits, main circuit main
module main (
  input  in_1,
  input  in_2,
  input  in_3,
  input  in_4,
  input  in_5,
  input  in_6,
  output out_7
);

  wire and_1_out, and_2_out, and_3_out, and_4_out, not_1_out, not_2_out;

  not not_1 (not_1_out, in_5);
  not not_2 (not_2_out, in_6);
  and and_1 (and_1_out, in_1, not_2_out, not_1_out);
  and and_2 (and_2_out, in_2, not_1_out, in_6);
  and and_3 (and_3_out, in_3, in_5, not_2_out);
  and and_4 (and_4_out, in_4, in_5, in_6);
  or or_1 (out_7, and_1_out, and_2_out, and_3_out, and_4_out);
endmodule

module _4_1mux (
  input  in_1,
  input  in_2,
  input  in_3,
  input  in_4,
  input  in_5,
  input  in_6,
  input  in_7,
  input  in_8,
  input  in_9,
  input  in_10,
  output out_11,
  output out_12,
  output out_13,
  output out_14,
  output out_15,
  output out_16,
  output out_17,
  output out_18,
  output out_19,
  output out_20,
  output out_21,
  output out_22,
  output out_23,
  output out_24,
  output out_25,
  output out_26,
  output out_27,
  output out_28,
  output out_29,
  output out_30
);

  and and_1 (out_11, in_1, in_2);
  or or_1 (out_12, in_1, in_2);
  not not_1 (out_14, in_1);
  xor xor_1 (out_15, in_1, in_2);
  and and_2 (out_16, in_3, in_4);
  or or_2 (out_17, in_3, in_4);
  not not_2 (out_19, in_3);
  xor xor_2 (out_20, in_3, in_4);
  and and_3 (out_21, in_7, in_8);
  or or_3 (out_22, in_7, in_8);
  not not_3 (out_24, in_7);
  xor xor_3 (out_25, in_7, in_8);
  and and_4 (out_26, in_9, in_10);
  or or_4 (out_27, in_9, in_10);
  not not_4 (out_29, in_9);
  xor xor_4 (out_30, in_9, in_10);
  main main_1 (.in_1(out_11), .in_2(out_12), .in_3(out_14), .in_4(out_15), .in_5(in_5), .in_6(in_6), .out_7(out_13));
  main main_2 (.in_1(out_16), .in_2(out_17), .in_3(out_19), .in_4(out_20), .in_5(in_5), .in_6(in_6), .out_7(out_18));
  main main_3 (.in_1(out_21), .in_2(out_22), .in_3(out_24), .in_4(out_25), .in_5(in_5), .in_6(in_6), .out_7(out_23));
  main main_4 (.in_1(out_26), .in_2(out_27), .in_3(out_29), .in_4(out_30), .in_5(in_5), .in_6(in_6), .out_7(out_28));
endmodule

module t (
  input  in_1,
  input  in_2,
  input  in_3,
  input  in_4,
  output out_5
);

  wire and_1_out, not_1_out, or_1_out, xor_1_out;

  and and_1 (and_1_out, in_1, in_2);
  or or_1 (or_1_out, in_1, in_2);
  not not_1 (not_1_out, in_1);
  xor xor_1 (xor_1_out, in_1, in_2);
  main main_1 (
    .in_1(and_1_out), .in_2(or_1_out), .in_3(not_1_out), .in_4(xor_1_out), .in_5(in_3), .in_6(in_4),
    .out_7(out_5));
endmodule

module r (
  input  in_1,
  input  in_2,
  input  in_3,
  input  in_4,
  input  in_5,
  input  in_6,
  input  in_7,
  input  in_8,
  input  in_9,
  input  in_10,
  input  in_11,
  input  in_12,
  input  in_13,
  input  in_14,
  input  in_15,
  input  in_16,
  input  in_17,
  input  in_18,
  input  in_19,
  input  in_20,
  input  in_21,
  input  in_22,
  input  in_23,
  input  in_24,
  input  in_25,
  input  in_26,
  input  in_27,
  input  in_28,
  input  in_29,
  input  in_30,
  input  in_31,
  input  in_32,
  output out_33,
  output out_34,
  output out_35,
  output out_36,
  output out_37,
  output out_38,
  output out_39,
  output out_40,
  output out_41,
  output out_42,
  output out_43,
  output out_44,
  output out_45,
  output out_46,
  output out_47,
  output out_48
);

  t t_1 (.in_1(in_1), .in_2(in_2), .out_5(out_33));  // open: in_3, in_4
  t t_2 (.in_1(in_3), .in_2(in_4), .out_5(out_34));  // open: in_3, in_4
  t t_3 (.in_1(in_5), .in_2(in_6), .out_5(out_35));  // open: in_3, in_4
  t t_4 (.in_1(in_7), .in_2(in_8), .out_5(out_36));  // open: in_3, in_4
  t t_5 (.in_1(in_9), .in_2(in_10), .out_5(out_37));  // open: in_3, in_4
  t t_6 (.in_1(in_11), .in_2(in_12), .out_5(out_38));  // open: in_3, in_4
  t t_7 (.in_1(in_13), .in_2(in_14), .out_5(out_39));  // open: in_3, in_4
  t t_8 (.in_1(in_15), .in_2(in_16), .out_5(out_40));  // open: in_3, in_4
  t t_9 (.in_1(in_17), .in_2(in_18), .out_5(out_41));  // open: in_3, in_4
  t t_10 (.in_1(in_19), .in_2(in_20), .out_5(out_42));  // open: in_3, in_4
  t t_11 (.in_1(in_21), .in_2(in_22), .out_5(out_43));  // open: in_3, in_4
  t t_12 (.in_1(in_23), .in_2(in_24), .out_5(out_44));  // open: in_3, in_4
  t t_13 (.in_1(in_25), .in_2(in_26), .out_5(out_45));  // open: in_3, in_4
  t t_14 (.in_1(in_27), .in_2(in_28), .out_5(out_46));  // open: in_3, in_4
  t t_15 (.in_1(in_29), .in_2(in_30), .out_5(out_47));  // open: in_3, in_4
  t t_16 (.in_1(in_31), .in_2(in_32), .out_5(out_48));  // open: in_3, in_4
endmodule
