// Logisim project 5_main.circ as structural Verilog: 4 circuits, main circuit main
module main (
  input  in_1,
  input  in_2,
  input  in_3,
  input  in_4,
  input  in_5,
  input  in_6,
  output out_7
);

  wire and_1_out, and_2_out, and_3_out, and_4_out, not_1_out, not_2_out;

  not not_1 (not_1_out, in_6);
  not not_2 (not_2_out, in_5);
  and and_1 (and_1_out, in_1, not_1_out, not_2_out);
  and and_2 (and_2_out, in_2, not_2_out, in_6);
  and and_3 (and_3_out, in_3, in_5, not_1_out);
  and and_4 (and_4_out, in_4, in_5, in_6);
  or or_1 (out_7, and_1_out, and_2_out, and_3_out, and_4_out);
endmodule

module _4_1mux (
  input  in_1,
  input  in_2,
  input  in_3,
  input  in_4,
  input  in_5,
  input  in_6,
  input  in_7,
  input  in_8,
  input  in_9,
  input  in_10,
  output out_11,
  output out_12,
  output out_13,
  output out_14,
  output out_15,
  output out_16,
  output out_17,
  output out_18,
  output out_19,
  output out_20,
  output out_21,
  output out_22,
  output out_23,
  output out_24,
  output out_25,
  output out_26,
  output out_27,
  output out_28,
  output out_29,
  output out_30
);

  and and_1 (out_11, in_1, in_2);
  or or_1 (out_12, in_1, in_2);
  not not_1 (out_14, in_1);
  xor xor_1 (out_15, in_1, in_2);
  and and_2 (out_16, in_3, in_4);
  or or_2 (out_17, in_3, in_4);
  not not_2 (out_19, in_3);
  xor xor_2 (out_20, in_3, in_4);
  and and_3 (out_21, in_7, in_8);
  or or_3 (out_22, in_7, in_8);
  not not_3 (out_24, in_7);
  xor xor_3 (out_25, in_7, in_8);
  and and_4 (out_26, in_9, in_10);
  or or_4 (out_27, in_9, in_10);
  not not_4 (out_29, in_9);
  xor xor_4 (out_30, in_9, in_10);
  main main_1 (.in_1(out_11), .in_2(out_12), .in_3(out_14), .in_4(out_15), .in_5(in_5), .in_6(in_6), .out_7(out_13));
  main main_2 (.in_1(out_16), .in_2(out_17), .in_3(out_19), .in_4(out_20), .in_5(in_5), .in_6(in_6), .out_7(out_18));
  main main_3 (.in_1(out_21), .in_2(out_22), .in_3(out_24), .in_4(out_25), .in_5(in_5), .in_6(in_6), .out_7(out_23));
  main main_4 (.in_1(out_26), .in_2(out_27), .in_3(out_29), .in_4(out_30), .in_5(in_5), .in_6(in_6), .out_7(out_28));
endmodule

module t (
  input  in_1,
  input  in_2,
  input  in_3,
  input  in_4,
  output out_5
);

  wire and_1_out, not_1_out, or_1_out, xor_1_out;

  and and_1 (and_1_out, in_1, in_2);
  or or_1 (or_1_out, in_1, in_2);
  not not_1 (not_1_out, in_1);
  xor xor_1 (xor_1_out, in_1, in_2);
  main main_1 (
    .in_1(and_1_out), .in_2(or_1_out), .in_3(not_1_out), .in_4(xor_1_out), .in_5(in_3), .in_6(in_4),
    .out_7(out_5));
endmodule

module r (
  input  in_1,
  input  in_2,
  input  in_3,
  input  in_4,
  input  in_5,
  input  in_6,
  input  in_7,
  input  in_8,
  input  in_9,
  input  in_10,
  input  in_11,
  input  in_12,
  input  in_13,
  input  in_14,
  input  in_15,
  input  in_16,
  input  in_17,
  input  in_18,
  input  in_19,
  input  in_20,
  input  in_21,
  input  in_22,
  input  in_23,
  input  in_24,
  input  in_25,
  input  in_26,
  input  in_27,
  input  in_28,
  input  in_29,
  input  in_30,
  input  in_31,
  input  in_32,
  input  in_33,
  input  in_34,
  input  in_35,
  input  in_36,
  input  in_37,
  input  in_38,
  input  in_39,
  input  in_40,
  input  in_41,
  input  in_42,
  input  in_43,
  input  in_44,
  input  in_45,
  input  in_46,
  input  in_47,
  input  in_48,
  input  in_49,
  input  in_50,
  input  in_51,
  input  in_52,
  input  in_53,
  input  in_54,
  input  in_55,
  input  in_56,
  input  in_57,
  input  in_58,
  input  in_59,
  input  in_60,
  input  in_61,
  input  in_62,
  input  in_63,
  input  in_64,
  input  in_65,
  input  in_66,
  output out_67,
  output out_68,
  output out_69,
  output out_70,
  output out_71,
  output out_72,
  output out_73,
  output out_74,
  output out_75,
  output out_76,
  output out_77,
  output out_78,
  output out_79,
  output out_80,
  output out_81,
  output out_82,
  output out_83,
  output out_84,
  output out_85,
  output out_86,
  output out_87,
  output out_88,
  output out_89,
  output out_90,
  output out_91,
  output out_92,
  output out_93,
  output out_94,
  output out_95,
  output out_96,
  output out_97,
  output out_98
);

  t t_1 (.in_1(in_1), .in_2(in_3), .in_3(in_66), .in_4(in_65), .out_5(out_67));
  t t_2 (.in_1(in_5), .in_2(in_7), .in_3(in_66), .in_4(in_65), .out_5(out_69));
  t t_3 (.in_1(in_9), .in_2(in_11), .in_3(in_66), .in_4(in_65), .out_5(out_71));
  t t_4 (.in_1(in_13), .in_2(in_15), .in_3(in_66), .in_4(in_65), .out_5(out_73));
  t t_5 (.in_1(in_17), .in_2(in_19), .in_3(in_66), .in_4(in_65), .out_5(out_75));
  t t_6 (.in_1(in_21), .in_2(in_23), .in_3(in_66), .in_4(in_65), .out_5(out_77));
  t t_7 (.in_1(in_25), .in_2(in_27), .in_3(in_66), .in_4(in_65), .out_5(out_79));
  t t_8 (.in_1(in_29), .in_2(in_31), .in_3(in_66), .in_4(in_65), .out_5(out_81));
  t t_9 (.in_1(in_33), .in_2(in_35), .in_3(in_66), .in_4(in_65), .out_5(out_83));
  t t_10 (.in_1(in_37), .in_2(in_39), .in_3(in_66), .in_4(in_65), .out_5(out_85));
  t t_11 (.in_1(in_41), .in_2(in_43), .in_3(in_66), .in_4(in_65), .out_5(out_87));
  t t_12 (.in_1(in_45), .in_2(in_47), .in_3(in_66), .in_4(in_65), .out_5(out_89));
  t t_13 (.in_1(in_49), .in_2(in_51), .in_3(in_66), .in_4(in_65), .out_5(out_91));
  t t_14 (.in_1(in_53), .in_2(in_55), .in_3(in_66), .in_4(in_65), .out_5(out_93));
  t t_15 (.in_1(in_57), .in_2(in_59), .in_3(in_66), .in_4(in_65), .out_5(out_95));
  t t_16 (.in_1(in_61), .in_2(in_63), .in_3(in_66), .in_4(in_65), .out_5(out_97));
  t t_17 (.in_1(in_2), .in_2(in_4), .in_3(in_66), .in_4(in_65), .out_5(out_68));
  t t_18 (.in_1(in_6), .in_2(in_8), .in_3(in_66), .in_4(in_65), .out_5(out_70));
  t t_19 (.in_1(in_10), .in_2(in_12), .in_3(in_66), .in_4(in_65), .out_5(out_72));
  t t_20 (.in_1(in_14), .in_2(in_16), .in_3(in_66), .in_4(in_65), .out_5(out_74));
  t t_21 (.in_1(in_18), .in_2(in_20), .in_3(in_66), .in_4(in_65), .out_5(out_76));
  t t_22 (.in_1(in_22), .in_2(in_24), .in_3(in_66), .in_4(in_65), .out_5(out_78));
  t t_23 (.in_1(in_26), .in_2(in_28), .in_3(in_66), .in_4(in_65), .out_5(out_80));
  t t_24 (.in_1(in_30), .in_2(in_32), .in_3(in_66), .in_4(in_65), .out_5(out_82));
  t t_25 (.in_1(in_34), .in_2(in_36), .in_3(in_66), .in_4(in_65), .out_5(out_84));
  t t_26 (.in_1(in_38), .in_2(in_40), .in_3(in_66), .in_4(in_65), .out_5(out_86));
  t t_27 (.in_1(in_42), .in_2(in_44), .in_3(in_66), .in_4(in_65), .out_5(out_88));
  t t_28 (.in_1(in_46), .in_2(in_48), .in_3(in_66), .in_4(in_65), .out_5(out_90));
  t t_29 (.in_1(in_50), .in_2(in_52), .in_3(in_66), .in_4(in_65), .out_5(out_92));
  t t_30 (.in_1(in_54), .in_2(in_56), .in_3(in_66), .in_4(in_65), .out_5(out_94));
  t t_31 (.in_1(in_58), .in_2(in_60), .in_3(in_66), .in_4(in_65), .out_5(out_96));
  t t_32 (.in_1(in_62), .in_2(in_64), .in_3(in_66), .in_4(in_65), .out_5(out_98));
endmodule
