// Logisim project 6.circ as structural Verilog: 1 circuit, main circuit main
module main (
  input  in_1,
  input  in_2,
  input  in_3,
  input  in_4,
  input  in_5,
  input  [1:0] in_6,
  output out_7,
  output out_8,
  output out_9,
  output out_10
);

  wire decoder_1_out0, decoder_1_out1, decoder_1_out2, decoder_1_out3;

  Decoder #(.select(2)) decoder_1 (
    .out0(decoder_1_out0), .out1(decoder_1_out1), .out2(decoder_1_out2), .out3(decoder_1_out3), .sel(in_6),
    .en(in_5));
  assign out_7 = decoder_1_out1 ? in_2 : 1'bz;  // Controlled_Buffer controlled_buffer_1
  assign out_7 = decoder_1_out0 ? in_1 : 1'bz;  // Controlled_Buffer controlled_buffer_2
  assign out_8 = decoder_1_out2 ? in_2 : 1'bz;  // Controlled_Buffer controlled_buffer_3
  assign out_8 = decoder_1_out1 ? in_1 : 1'bz;  // Controlled_Buffer controlled_buffer_4
  assign out_9 = decoder_1_out3 ? in_2 : 1'bz;  // Controlled_Buffer controlled_buffer_5
  assign out_9 = decoder_1_out2 ? in_1 : 1'bz;  // Controlled_Buffer controlled_buffer_6
  assign out_10 = decoder_1_out3 ? in_1 : 1'bz;  // Controlled_Buffer controlled_buffer_7
  assign out_10 = decoder_1_out0 ? in_2 : 1'bz;  // Controlled_Buffer controlled_buffer_8
  assign out_7 = decoder_1_out2 ? in_3 : 1'bz;  // Controlled_Buffer controlled_buffer_9
  assign out_8 = decoder_1_out3 ? in_3 : 1'bz;  // Controlled_Buffer controlled_buffer_10
  assign out_9 = decoder_1_out0 ? in_3 : 1'bz;  // Controlled_Buffer controlled_buffer_11
  assign out_10 = decoder_1_out1 ? in_3 : 1'bz;  // Controlled_Buffer controlled_buffer_12
  assign out_7 = decoder_1_out3 ? in_4 : 1'bz;  // Controlled_Buffer controlled_buffer_13
  assign out_8 = decoder_1_out0 ? in_4 : 1'bz;  // Controlled_Buffer controlled_buffer_14
  assign out_9 = decoder_1_out1 ? in_4 : 1'bz;  // Controlled_Buffer controlled_buffer_15
  assign out_10 = decoder_1_out2 ? in_4 : 1'bz;  // Controlled_Buffer controlled_buffer_16
endmodule
